# Fritzing sketch led_apt_stairs_arduino (saved by Fritzing 0.9.3b)
breadboards: 1

parts:
  U1 = Voltage Regulator - 5V [package="TO220 [THT]"]
  Q1 = TIP120 Hi-Current Darlington Transistor
  Q2 = TIP120 Hi-Current Darlington Transistor
  Q3 = TIP120 Hi-Current Darlington Transistor
  Part1 = Arduino Uno (Rev3)
  Part2 = Ambient Light Sensor (TEMT6000 Breakout Board)
  R1 = Resistor [tolerance=±5% resistance=100 package=THT]
  R2 = Resistor [tolerance=±5% resistance=100 package=THT]
  R3 = Resistor [tolerance=±5% resistance=100 package=THT]
  R4 = Resistor [tolerance=±5% resistance=1.5k package=THT]
  R5 = Resistor [tolerance=±5% resistance=3.3k package=THT]
  U2 = Tri-Color LED SMD [package=led-tricolor-smd]  # not connected

nets:
  N1: U1.GND, Q1.EMITTER, Q2.EMITTER, Q3.EMITTER
  N2: U1.output_voltage, Part2.S, R4.Pin_1
  N3: Q1.BASE, R2.Pin_0
  N4: Q2.BASE, R3.Pin_0
  N5: Q3.BASE, R1.Pin_0
  N6: Part1.A0, Part2.GND
  N7: Part1.D9_PWM, R3.Pin_1
  N8: Part1.D10_PWM/SS, R2.Pin_1
  N9: Part1.D11_PWM/MOSI, R1.Pin_1
  N10: Part1.AREF, R4.Pin_0, R5.Pin_0
  N11: Part2.VCC, R5.Pin_1
